# Fritzing sketch PresensiRFID (saved by Fritzing 0.8.7b)
breadboards: 1

parts:
  Part1 = Arduino Mega ADK (Rev3)
  J1 = Piezo Speaker
  LCD1 = LCD screen
  R1 = Resistor [tolerance=±5% resistance=3.3k package=THT]
  Part2 = RFID-RC522-v2

nets:
  N1: Part1.D12_PWM, Part2.MISO
  N2: Part1.D10_PWM, Part2.SDA
  N3: Part1.D9_PWM, Part2.RST
  N4: Part1.D8_PWM, J1.pin2
  3V3: Part1.3V3, Part2.3.3V
  5V: Part1.5V, LCD1.VDD, LCD1.LED+, R1.Pin_0
  GND: Part1.GND, J1.pin1, LCD1.VSS, LCD1.R/W, LCD1.LED-, Part2.GND
  N5: Part1.D2_PWM, LCD1.RS
  N6: Part1.D3_PWM, LCD1.E
  N7: LCD1.V0, R1.Pin_1

custom parts:
  RFID-RC522-v2: A simple China made RFID-RC522 Reader; do check the pin labels, as this is a MFRC522 based clone.
