# Fritzing sketch PresensiRFID_I2C (saved by Fritzing 0.8.7b)
breadboards: 1

parts:
  Part1 = Arduino Mega ADK (Rev3)
  J1 = Piezo Speaker
  LCD1 = LCD screen
  Part2 = RFID-RC522-v2
  LCM1602_IIC1 = LCM1602 IIC [part_number="LCM1602 IIC" chip_label="LCM1602 IIC" package="DIP (Dual Inline) [THT]"]

nets:
  N1: Part1.A4, LCM1602_IIC1.SDA
  N2: Part1.A5, LCM1602_IIC1.SCL
  N3: Part1.D12_PWM, Part2.MISO
  N4: Part1.D10_PWM, Part2.SDA
  N5: Part1.D9_PWM, Part2.RST
  N6: Part1.D8_PWM, J1.pin2
  3V3: Part1.3V3, Part2.3.3V
  5V: Part1.5V, LCM1602_IIC1.VCC
  GND: Part1.GND, J1.pin1, Part2.GND, LCM1602_IIC1.GND
  VSS: LCD1.VSS, LCM1602_IIC1.VSS
  VDD: LCD1.VDD, LCM1602_IIC1.VDD
  N7: LCD1.V0, LCM1602_IIC1.V0
  N8: LCD1.RS, LCM1602_IIC1.RS
  N9: LCD1.R/W, LCM1602_IIC1.RW
  N10: LCD1.E, LCM1602_IIC1.E
  N11: LCD1.DB0, LCM1602_IIC1.D0
  N12: LCD1.DB1, LCM1602_IIC1.D1
  N13: LCD1.DB2, LCM1602_IIC1.D2
  N14: LCD1.DB3, LCM1602_IIC1.D3
  N15: LCD1.DB4, LCM1602_IIC1.D4
  N16: LCD1.DB5, LCM1602_IIC1.D5
  N17: LCD1.DB6, LCM1602_IIC1.D6
  N18: LCD1.DB7, LCM1602_IIC1.D7
  N19: LCD1.LED+, LCM1602_IIC1.A
  N20: LCD1.LED-, LCM1602_IIC1.K

custom parts:
  RFID-RC522-v2: A simple China made RFID-RC522 Reader; do check the pin labels, as this is a MFRC522 based clone.
  LCM1602 IIC: I2C-Module to use a 1602 or 2004 LCD on with the wire.h libory Serial LCD Modul
